// Logisim project Ctl_Conditional.circ as structural Verilog: 1 circuit, main circuit Conditional
module Conditional (
  input  Enable,
  input  [15:0] Instruction,
  input  Z,
  input  C,
  input  N,
  input  V,
  output [10:0] Offset,
  output Verified
);

  wire multiplexer_1_out, o_CC_LO, o_CS_HS, o_GE, o_GT, o_HI, o_LE, o_LS, o_LT, o_MI, o_NE, o_PL, o_VC, o_VS,
       or_3_out;
  wire [10:0] bit_extender_1_out, multiplexer_2_out;

  and and_1 (o_CS_HS, C, 1'b1);
  and and_2 (o_MI, N, 1'b1);
  and and_3 (o_VS, V, 1'b1);
  and and_4 (o_HI, o_CS_HS, o_NE);
  or or_1 (o_LS, o_CC_LO, Z);
  not not_1 (o_LT, o_GE);
  and and_5 (o_GT, o_GE, o_NE);
  or or_2 (o_LE, Z, o_LT);
  not not_2 (o_NE, Z);
  xnor xnor_1 (o_CC_LO, C, 1'b0);
  xnor xnor_2 (o_PL, N, 1'b0);
  xnor xnor_3 (o_VC, V, 1'b0);
  xnor xnor_4 (o_GE, N, V);
  Multiplexer #(.enable("false"), .select(4)) multiplexer_1 (
    .in0(Z), .in1(o_NE), .in2(o_CS_HS), .in3(o_CC_LO), .in4(o_MI), .in5(o_PL), .in6(o_VS), .in7(o_VC),
    .in8(o_HI), .in9(o_LS), .in10(o_GE), .in11(o_LT), .in12(o_GT), .in13(o_LE), .in14(1'b1),
    .out(multiplexer_1_out), .sel(Instruction[11:8]));  // open: in15
  // Probe on Instruction[11:8]
  or or_3 (or_3_out, Instruction[13], multiplexer_1_out);
  assign bit_extender_1_out = {{3{Instruction[7]}}, Instruction[7:0]};  // Bit_Extender bit_extender_1
  and and_6 (Verified, Enable, or_3_out);
  Multiplexer #(.enable("false"), .width(11)) multiplexer_2 (
    .in0(bit_extender_1_out), .in1(Instruction[10:0]), .out(multiplexer_2_out), .sel(Instruction[13]));
  Multiplexer #(.enable("false"), .width(11)) multiplexer_3 (
    .in0({11{1'b0}}), .in1(multiplexer_2_out), .out(Offset), .sel(Verified));

  // Other names for the same wires on the sheet: imm8[7:0] = Instruction[7:0]; imm11[10:0] = Instruction[10:0];
  //   cond[3:0] = Instruction[11:8]; incond = Instruction[13]; o_EQ = Z
endmodule
