// Logisim project Ctl_Shift_Add_Sub_Mov.circ as structural Verilog: 2 circuits, main circuit Shift_Add_Sub_Mov
module Shift_Add_Sub_Mov (
  input  Enable,
  input  [15:0] Instruction,
  output [3:0] Flags_Update_Mask,
  output Carry,
  output Imm32_Enable,
  output [2:0] Rm,
  output [2:0] Rn,
  output [2:0] Rd,
  output [4:0] Imm5,
  output [31:0] Imm32,
  output [3:0] ALU_Opcode
);

  wire add_i, add_r, and_1_out, and_2_out, i_AD, i_ADD, i_ASR, i_CMP, i_LSL, i_LSR, i_MOV, i_SUB, or_1_out,
       or_2_out, or_3_out, or_4_out, sub_i, sub_r;
  wire [2:0] imm3;
  wire [7:0] imm8;
  wire [15:0] bit_extender_1_out, bit_extender_2_out, bit_extender_3_out, bit_extender_4_out,
       bit_extender_5_out, INST;
  wire [15:9] and_5_out, and_6_out;
  wire [15:11] and_4_out, and_7_out;

  Decoder #(.select(3)) decoder_1 (
    .out0(i_LSL), .out1(i_LSR), .out2(i_ASR), .out3(i_AD), .out4(i_MOV), .out5(i_CMP), .out6(i_ADD),
    .out7(i_SUB), .sel(INST[13:11]));  // open: en
  Decoder #(.select(2)) decoder_2 (
    .out0(add_r), .out1(sub_r), .out2(add_i), .out3(sub_i), .sel(INST[10:9]));  // open: en
  or or_1 (or_1_out, i_LSL, i_LSR, i_ASR);
  or or_2 (or_2_out, add_r, sub_r);
  or or_3 (or_3_out, add_i, sub_i);
  assign bit_extender_1_out = {{15{Enable}}, Enable};  // Bit_Extender bit_extender_1
  assign bit_extender_2_out = {{15{or_1_out}}, or_1_out};  // Bit_Extender bit_extender_2
  and and_1 (and_1_out, i_AD, or_2_out);
  and and_2 (and_2_out, i_AD, or_3_out);
  or or_4 (or_4_out, i_MOV, i_CMP, i_ADD, i_SUB);
  assign INST = Instruction & bit_extender_1_out;  // AND_Gate and_3, 16 bits wide
  assign {and_4_out, Imm5, Rm, Rd} = bit_extender_2_out & INST;  // AND_Gate and_4, 16 bits wide
  assign bit_extender_3_out = {{15{and_1_out}}, and_1_out};  // Bit_Extender bit_extender_3
  assign bit_extender_4_out = {{15{and_2_out}}, and_2_out};  // Bit_Extender bit_extender_4
  assign bit_extender_5_out = {{15{or_4_out}}, or_4_out};  // Bit_Extender bit_extender_5
  assign {and_5_out, Rm, Rn, Rd} = bit_extender_3_out & INST;  // AND_Gate and_5, 16 bits wide
  assign {and_6_out, imm3, Rn, Rd} = bit_extender_4_out & INST;  // AND_Gate and_6, 16 bits wide
  assign {and_7_out, Rd, imm8} = bit_extender_5_out & INST;  // AND_Gate and_7, 16 bits wide
  assign Imm32 = {{29{imm3[2]}}, imm3};  // Bit_Extender bit_extender_6
  Flags_To_Update flags_to_update_1 (.codop(INST[13:11]), .flags_update_mask(Flags_Update_Mask));

  // Notes on the sheet:
  //   Pull output low on Enable = 0
  //   only ADD and SUB use Rm
  //   Enable carry for SUB since it is reversed in ALU
  //   ALU will use Imm32 instead of Rm
endmodule

module Flags_To_Update (
  input  [2:0] codop,
  output [3:0] flags_update_mask
);

  wire and_1_out, and_2_out, and_3_out, not_1_out;

  not not_1 (not_1_out, codop[2]);
  or or_1 (flags_update_mask[1], not_1_out, codop[0], codop[1]);
  and and_1 (and_1_out, codop[1], codop[0]);
  and and_2 (and_2_out, codop[2], codop[0]);
  and and_3 (and_3_out, codop[2], codop[1]);
  or or_2 (flags_update_mask[0], and_1_out, and_2_out, and_3_out);

  assign flags_update_mask[3:2] = 2'b11;
endmodule
